# Fritzing sketch Schematics (saved by Fritzing 0.9.5d)
breadboards: 1

parts:
  Компонент1 = Arduino Uno (Rev3) - ICSP
  ACC_PIN_17_(BUS+) = female pin header, 1 pin [form="♀ (female)"]
  PIN_7_(GND) = female pin header, 1 pin [form="♀ (female)"]
  D1 = Schottky Diode [part_number=1N5817 package="300 mil [THT]"]
  FRONT_PANEL_CHIP_15_(ROW) = female pin header, 1 pin [form="♀ (female)"]
  D2 = Schottky Diode [part_number=1N5817 package="300 mil [THT]"]
  R1 = Resistor [tolerance=±5% resistance=220 package=THT]
  D3 = Schottky Diode [part_number=1N5817 package="300 mil [THT]"]
  R2 = Resistor [tolerance=±5% resistance=220 package=THT]
  D4 = Schottky Diode [part_number=1N5817 package="300 mil [THT]"]
  R3 = Resistor [tolerance=±5% resistance=220 package=THT]

nets:
  N1: Компонент1.ICSP_MOSI, Компонент1.D11_PWM/MOSI, D4.cathode
  N2: Компонент1.D8, D1.cathode
  N3: Компонент1.D9_PWM, D2.cathode
  N4: Компонент1.D10_PWM/SS, D3.cathode
  N5: Компонент1.D2, ACC_PIN_17_(BUS+).pin1
  N6: Компонент1.GND, PIN_7_(GND).pin1
  N7: D1.anode, FRONT_PANEL_CHIP_15_(ROW).pin1, R1.Pin_1
  N8: D2.anode, R1.Pin_0, R2.Pin_1
  N9: D3.anode, R2.Pin_0, R3.Pin_1
  N10: D4.anode, R3.Pin_0
